// Logisim project CPU.circ as structural Verilog: 7 circuits, main circuit ExampleConfigurationROM
module MCU (
  input  IO_ENABLE,
  input  [7:0] IN,
  input  CLK,
  input  RST,
  output IO_ACTIVE,
  output WRITE_ACTIVE,
  output [7:0] OUT,
  output [7:0] ADDR
);

  wire alu_1_flag, and_1_out, and_2_out, isd_1_address_mux, isd_1_alu_state, isd_1_gpr_forward_input,
       isd_1_memory_select, isd_1_pop, isd_1_push;
  wire [1:0] isd_1_a__r, isd_1_b__r, isd_1_branch, isd_1_c__w, isd_1_gpr_mux;
  wire [2:0] isd_1_alu_op;
  wire [3:0] isd_1_dynamic_op;
  wire [7:0] gpr_1_read_a_2, gpr_1_read_b_2, isd_1_imm_value, isd_1_mem_pointer, multiplexer_2_out,
       multiplexer_3_out, pc_1_out_7, pc_1_out_8, ram_1_data, stk_1_out_6;

  STK stk_1 (.out_6(stk_1_out_6), .in_1(OUT), .in_2(CLK), .in_4(isd_1_pop), .in_5(isd_1_push), .in_3(RST));
  ISD isd_1 (
    .DATA(multiplexer_3_out), .CLK(CLK), .RST(RST), .ALU_OP(isd_1_alu_op), .GPR_MUX(isd_1_gpr_mux),
    .Address_MUX(isd_1_address_mux), .POP(isd_1_pop), .PUSH(isd_1_push), .A__R(isd_1_a__r),
    .B__R(isd_1_b__r), .C__W(isd_1_c__w), .Write_Enable(WRITE_ACTIVE), .BRANCH(isd_1_branch),
    .JMP_FLAG(alu_1_flag), .ALU_OUTPUT(OUT), .MEM_POINTER(isd_1_mem_pointer), .PC_ADDRESS(pc_1_out_7),
    .IMM_VALUE(isd_1_imm_value), .Dynamic_OP(isd_1_dynamic_op), .ALU_State(isd_1_alu_state),
    .Memory_Select(isd_1_memory_select), .External_Address_Select(IO_ACTIVE),
    .GPR_Forward_Input(isd_1_gpr_forward_input));
  PC pc_1 (
    .DATA(multiplexer_3_out), .Jump_Enable(isd_1_branch), .out_8(pc_1_out_8), .in_6(RST), .out_7(pc_1_out_7),
    .in_4(isd_1_address_mux), .in_5(CLK), .ALU(OUT));
  Multiplexer #(.width(8), .enable("false")) multiplexer_1 (
    .in0(pc_1_out_8), .in1(isd_1_mem_pointer), .out(ADDR), .sel(isd_1_address_mux));
  Multiplexer #(.select(2), .width(8), .enable("false")) multiplexer_2 (
    .in0(OUT), .in1(multiplexer_3_out), .in2(stk_1_out_6), .in3(isd_1_imm_value), .out(multiplexer_2_out),
    .sel(isd_1_gpr_mux));
  ALU alu_1 (
    .out_6(OUT), .STATIC_OPCODE(isd_1_alu_op), .in_1(gpr_1_read_a_2), .in_2(gpr_1_read_b_2),
    .FLAG(alu_1_flag), .DYN_OP(isd_1_dynamic_op), .ALU_STATE(isd_1_alu_state));
  GPR gpr_1 (
    .Input(multiplexer_2_out), .Read_A_2(gpr_1_read_a_2), .Read_B_2(gpr_1_read_b_2), .Read_A(isd_1_b__r),
    .Read_B(isd_1_a__r), .in_2(CLK), .in_4(RST), .Forward_Input_A(isd_1_gpr_forward_input), .Write(isd_1_c__w));
  and and_1 (and_1_out, WRITE_ACTIVE, CLK);
  RAM #(.bus("separate")) ram_1 (
    .addr(ADDR), .din(OUT), .data(ram_1_data), .sel(1'b1), .clk(and_1_out), .clr(RST));  // open: str, ld
  Multiplexer #(.width(8), .enable("false")) multiplexer_3 (
    .in0(ram_1_data), .in1(IN), .out(multiplexer_3_out), .sel(and_2_out));
  and and_2 (and_2_out, ~isd_1_memory_select, IO_ENABLE);  // AND_Gate

  // Notes on the sheet:
  //   RST: pull=down
  //   ADDR: pull=down
  //   OUT: pull=down
  //   IN: pull=down
  //   CLK: pull=down
  //   IO_ENABLE: pull=down
  //   TISCv2.3
endmodule

module ALU (
  input  [7:0] in_1,
  input  [7:0] in_2,
  input  [2:0] STATIC_OPCODE,
  input  ALU_STATE,
  input  [3:0] DYN_OP,
  output [7:0] out_6,
  output FLAG
);

  wire and_1_out, and_2_out, and_3_out, and_4_out, and_5_out, and_6_out, and_7_out, and_8_out, and_9_out,
       and_10_out, and_11_out, and_12_out, and_13_out, and_14_out, and_15_out, and_16_out, and_17_out,
       and_18_out, and_19_out, and_20_out, and_21_out, and_22_out, and_23_out, and_24_out, and_25_out,
       and_26_out, and_27_out, and_28_out, and_29_out, and_30_out, and_31_out, and_32_out, and_33_out, CC,
       CI, comparator_1_gt, FC, nA, nB, nor_1_out, nor_2_out, nor_3_out, nor_4_out, nor_5_out, nor_6_out,
       nor_7_out, nor_8_out, o0, o1, o2, o3, o4, o5, o6, o7, OR, or_1_out, or_2_out, or_3_out, or_4_out,
       or_5_out, or_6_out, or_7_out, or_8_out, or_9_out, or_10_out, or_11_out, or_12_out, or_13_out,
       or_14_out, or_15_out, or_16_out, or_17_out, or_18_out, or_19_out, or_20_out, or_21_out, or_22_out,
       or_23_out, or_24_out, or_25_out, or_26_out, xor_1_out, xor_2_out, xor_3_out, xor_4_out, xor_5_out,
       xor_6_out, xor_7_out, xor_8_out, xor_9_out, xor_10_out, xor_11_out, xor_12_out, xor_13_out,
       xor_14_out, xor_15_out, xor_16_out;
  wire [2:0] multiplexer_3_out, rom_1_data;
  wire [3:0] bitadder_1_out, bitadder_2_out;
  wire [6:3] rom_1_data_2;
  wire [7:0] multiplexer_4_out, multiplexer_5_out, multiplexer_6_out, shifter_1_out, shifter_2_out;

  xor xor_1 (xor_1_out, in_1[0], nB);
  xor xor_2 (xor_2_out, in_2[0], nA);
  xor xor_3 (xor_3_out, in_1[1], nB);
  xor xor_4 (xor_4_out, in_2[1], nA);
  xor xor_5 (xor_5_out, in_1[2], nB);
  xor xor_6 (xor_6_out, in_2[2], nA);
  xor xor_7 (xor_7_out, in_1[3], nB);
  xor xor_8 (xor_8_out, in_2[3], nA);
  xor xor_9 (xor_9_out, in_1[4], nB);
  xor xor_10 (xor_10_out, in_2[4], nA);
  xor xor_11 (xor_11_out, in_1[5], nB);
  xor xor_12 (xor_12_out, in_2[5], nA);
  xor xor_13 (xor_13_out, in_1[6], nB);
  xor xor_14 (xor_14_out, in_2[6], nA);
  xor xor_15 (xor_15_out, in_1[7], nB);
  xor xor_16 (xor_16_out, in_2[7], nA);
  nor nor_1 (nor_1_out, xor_1_out, xor_2_out);
  or or_1 (or_1_out, nor_1_out, and_2_out);
  and and_1 (and_1_out, xor_1_out, xor_2_out);
  and and_2 (and_2_out, and_1_out, ~OR);  // AND_Gate
  or or_2 (or_2_out, and_25_out, FC);
  and and_3 (and_3_out, and_2_out, ~CC);  // AND_Gate
  or or_3 (or_3_out, and_3_out, or_2_out);
  nor nor_2 (nor_2_out, xor_3_out, xor_4_out);
  or or_4 (or_4_out, nor_2_out, and_5_out);
  and and_4 (and_4_out, xor_3_out, xor_4_out);
  and and_5 (and_5_out, and_4_out, ~OR);  // AND_Gate
  and and_6 (and_6_out, and_5_out, ~CC);  // AND_Gate
  or or_5 (or_5_out, and_26_out, FC);
  or or_6 (or_6_out, and_6_out, or_5_out);
  nor nor_3 (nor_3_out, xor_5_out, xor_6_out);
  or or_7 (or_7_out, nor_3_out, and_8_out);
  and and_7 (and_7_out, xor_5_out, xor_6_out);
  and and_8 (and_8_out, and_7_out, ~OR);  // AND_Gate
  or or_8 (or_8_out, and_27_out, FC);
  and and_9 (and_9_out, and_8_out, ~CC);  // AND_Gate
  or or_9 (or_9_out, and_9_out, or_8_out);
  nor nor_4 (nor_4_out, xor_7_out, xor_8_out);
  or or_10 (or_10_out, nor_4_out, and_11_out);
  and and_10 (and_10_out, xor_7_out, xor_8_out);
  and and_11 (and_11_out, and_10_out, ~OR);  // AND_Gate
  or or_11 (or_11_out, and_28_out, FC);
  and and_12 (and_12_out, and_11_out, ~CC);  // AND_Gate
  or or_12 (or_12_out, and_12_out, or_11_out);
  nor nor_5 (nor_5_out, xor_9_out, xor_10_out);
  or or_13 (or_13_out, nor_5_out, and_14_out);
  and and_13 (and_13_out, xor_9_out, xor_10_out);
  and and_14 (and_14_out, and_13_out, ~OR);  // AND_Gate
  or or_14 (or_14_out, and_29_out, FC);
  and and_15 (and_15_out, and_14_out, ~CC);  // AND_Gate
  or or_15 (or_15_out, and_15_out, or_14_out);
  nor nor_6 (nor_6_out, xor_11_out, xor_12_out);
  or or_16 (or_16_out, nor_6_out, and_17_out);
  and and_16 (and_16_out, xor_11_out, xor_12_out);
  and and_17 (and_17_out, and_16_out, ~OR);  // AND_Gate
  and and_18 (and_18_out, and_17_out, ~CC);  // AND_Gate
  or or_17 (or_17_out, and_30_out, FC);
  or or_18 (or_18_out, and_18_out, or_17_out);
  nor nor_7 (nor_7_out, xor_13_out, xor_14_out);
  or or_19 (or_19_out, nor_7_out, and_20_out);
  and and_19 (and_19_out, xor_13_out, xor_14_out);
  and and_20 (and_20_out, and_19_out, ~OR);  // AND_Gate
  and and_21 (and_21_out, and_20_out, ~CC);  // AND_Gate
  or or_20 (or_20_out, and_31_out, FC);
  or or_21 (or_21_out, and_21_out, or_20_out);
  nor nor_8 (nor_8_out, xor_15_out, xor_16_out);
  or or_22 (or_22_out, nor_8_out, and_23_out);
  and and_22 (and_22_out, xor_15_out, xor_16_out);
  and and_23 (and_23_out, and_22_out, ~OR);  // AND_Gate
  and and_24 (and_24_out, and_23_out, ~CC);  // AND_Gate
  or or_23 (or_23_out, and_32_out, FC);
  or or_24 (or_24_out, and_24_out, or_23_out);
  xnor xnor_1 (o0, CI, or_1_out);
  and and_25 (and_25_out, CI, ~or_1_out);  // AND_Gate
  xnor xnor_2 (o1, or_3_out, or_4_out);
  and and_26 (and_26_out, or_3_out, ~or_4_out);  // AND_Gate
  xnor xnor_3 (o2, or_6_out, or_7_out);
  and and_27 (and_27_out, or_6_out, ~or_7_out);  // AND_Gate
  xnor xnor_4 (o3, or_9_out, or_10_out);
  and and_28 (and_28_out, or_9_out, ~or_10_out);  // AND_Gate
  xnor xnor_5 (o4, or_12_out, or_13_out);
  and and_29 (and_29_out, or_12_out, ~or_13_out);  // AND_Gate
  xnor xnor_6 (o5, or_15_out, or_16_out);
  and and_30 (and_30_out, or_15_out, ~or_16_out);  // AND_Gate
  xnor xnor_7 (o6, or_18_out, or_19_out);
  and and_31 (and_31_out, or_18_out, ~or_19_out);  // AND_Gate
  xnor xnor_8 (o7, or_21_out, or_22_out);
  and and_32 (and_32_out, or_21_out, ~or_22_out);  // AND_Gate
  Multiplexer #(.select(2), .enable("false")) multiplexer_1 (
    .in0(or_24_out), .in1(or_26_out), .in2(comparator_1_gt), .in3(1'b0), .out(FLAG), .sel(rom_1_data_2[4:3]));
  Multiplexer #(.width(8), .enable("false")) multiplexer_2 (
    .in0({o7, o6, o5, o4, o3, o2, o1, o0}), .in1(multiplexer_6_out), .out(out_6), .sel(and_33_out));
  and and_33 (and_33_out, or_25_out, ALU_STATE);
  Multiplexer #(.width(3), .enable("false")) multiplexer_3 (
    .in0(STATIC_OPCODE), .in1(rom_1_data), .out(multiplexer_3_out), .sel(ALU_STATE));
  ROM #(.addrWidth(4), .dataWidth(7)) rom_1 (.addr(DYN_OP), .data({rom_1_data_2, rom_1_data}));  // open: sel
  ROM #(.addrWidth(3), .dataWidth(6)) rom_2 (.addr(multiplexer_3_out), .data({nA, nB, OR, CC, CI, FC}), .sel(1'b1));
  or or_25 (or_25_out, rom_1_data_2[5], rom_1_data_2[6]);
  Multiplexer #(.width(8), .enable("false")) multiplexer_4 (
    .in0({8{1'b0}}), .in1(in_2), .out(multiplexer_4_out), .sel(or_25_out));
  Multiplexer #(.width(8), .enable("false")) multiplexer_5 (
    .in0({8{1'b0}}), .in1(in_1), .out(multiplexer_5_out), .sel(or_25_out));
  or or_26 (or_26_out, o0, o1, o2, o3, o4, o5, o6, o7);
  BitAdder bitadder_1 (.in0(multiplexer_4_out), .out(bitadder_1_out));
  Shifter shifter_1 (.in(multiplexer_4_out), .\dist (multiplexer_5_out[2:0]), .out(shifter_1_out));
  Shifter #(.shift("lr")) shifter_2 (.in(multiplexer_4_out), .\dist (multiplexer_5_out[2:0]), .out(shifter_2_out));
  BitAdder bitadder_2 (.in0(multiplexer_6_out), .out(bitadder_2_out));
  Multiplexer #(.width(8), .enable("false")) multiplexer_6 (
    .in0(shifter_1_out), .in1(shifter_2_out), .out(multiplexer_6_out), .sel(rom_1_data_2[6]));
  Comparator #(.width(4)) comparator_1 (.a(bitadder_1_out), .b(bitadder_2_out), .gt(comparator_1_gt));  // open: eq, lt

  // Other names for the same wires on the sheet: A[7:0] = in_2; a0 = in_2[0]; a1 = in_2[1]; a2 = in_2[2];
  //   a3 = in_2[3]; a4 = in_2[4]; a5 = in_2[5]; a6 = in_2[6]; a7 = in_2[7]; B[7:0] = in_1; b0 = in_1[0]; b1 = in_1[1];
  //   b2 = in_1[2]; b3 = in_1[3]; b4 = in_1[4]; b5 = in_1[5]; b6 = in_1[6]; b7 = in_1[7]

  // Notes on the sheet:
  //   Output
  //   Input B
  //   Opcodes
  //   contents of rom_1 (hex, n*v repeats v):
  //   3 7 9 a 6 4 30 50
  //   Input A
  //   contents of rom_2 (hex, n*v repeats v):
  //   8 3b 4 0 2 38 7 12
  //   OPCODES: 000: OR, 001: AND, 010: XOR, 011: ADD, 100: CIN, 101: NAND, 110: XNOR, 111: SUB
endmodule

module GPR (
  input  [1:0] Write,
  input  in_2,
  input  [7:0] Input,
  input  in_4,
  input  Forward_Input_A,
  input  [1:0] Read_A,
  input  [1:0] Read_B,
  output [7:0] Read_A_2,
  output [7:0] Read_B_2
);

  wire decoder_1_out0, decoder_1_out1, decoder_1_out2, decoder_1_out3, decoder_2_out1, decoder_2_out2,
       decoder_2_out3, decoder_3_out0, decoder_3_out1, decoder_3_out2, decoder_3_out3;
  wire [7:0] multiplexer_1_out, register_1_q, register_2_q, register_3_q;

  Decoder #(.select(2), .enable("false")) decoder_1 (
    .out0(decoder_1_out0), .out1(decoder_1_out1), .out2(decoder_1_out2), .out3(decoder_1_out3), .sel(Read_A));
  Decoder #(.select(2), .enable("false")) decoder_2 (
    .out1(decoder_2_out1), .out2(decoder_2_out2), .out3(decoder_2_out3), .sel(Write));  // open: out0
  Register register_1 (.D(Input), .en(decoder_2_out2), .Q(register_1_q), .clk(in_2), .clr(in_4));
  Register register_2 (.D(Input), .en(decoder_2_out1), .Q(register_2_q), .clk(in_2), .clr(in_4));
  assign Read_A_2 = decoder_1_out1 ? register_2_q : 8'bz;  // Controlled_Buffer controlled_buffer_1
  assign Read_A_2 = decoder_1_out2 ? register_1_q : 8'bz;  // Controlled_Buffer controlled_buffer_2
  assign Read_B_2 = decoder_3_out1 ? register_2_q : 8'bz;  // Controlled_Buffer controlled_buffer_3
  assign Read_B_2 = decoder_3_out2 ? register_1_q : 8'bz;  // Controlled_Buffer controlled_buffer_4
  Register register_3 (.D(Input), .en(decoder_2_out3), .Q(register_3_q), .clk(in_2), .clr(in_4));
  assign Read_A_2 = decoder_1_out0 ? multiplexer_1_out : 8'bz;  // Controlled_Buffer controlled_buffer_5
  assign Read_A_2 = decoder_1_out3 ? register_3_q : 8'bz;  // Controlled_Buffer controlled_buffer_6
  assign Read_B_2 = decoder_3_out3 ? register_3_q : 8'bz;  // Controlled_Buffer controlled_buffer_7
  assign Read_B_2 = decoder_3_out0 ? {8{1'b0}} : 8'bz;  // Controlled_Buffer controlled_buffer_8
  Decoder #(.select(2), .enable("false")) decoder_3 (
    .out0(decoder_3_out0), .out1(decoder_3_out1), .out2(decoder_3_out2), .out3(decoder_3_out3), .sel(Read_B));
  Multiplexer #(.width(8), .enable("false")) multiplexer_1 (
    .in0({8{1'b0}}), .in1(Input), .out(multiplexer_1_out), .sel(Forward_Input_A));
endmodule

module ISD (
  input  [7:0] DATA,
  input  CLK,
  input  RST,
  input  [7:0] ALU_OUTPUT,
  input  [7:0] PC_ADDRESS,
  input  JMP_FLAG,
  output Write_Enable,
  output ALU_State,
  output GPR_Forward_Input,
  output [1:0] GPR_MUX,
  output POP,
  output PUSH,
  output [1:0] A__R,
  output [1:0] B__R,
  output [1:0] C__W,
  output [2:0] ALU_OP,
  output [3:0] Dynamic_OP,
  output [7:0] MEM_POINTER,
  output [7:0] IMM_VALUE,
  output Memory_Select,
  output Address_MUX,
  output [1:0] BRANCH,
  output External_Address_Select
);

  wire and_1_out, and_2_out, and_3_out, and_4_out, and_6_out, and_8_out, and_9_out, and_11_out, and_12_out,
       and_13_out, and_14_out, and_15_out, and_16_out, and_17_out, CIN_out, CMP_out, comparator_1_lt,
       comparator_2_eq, comparator_2_gt, comparator_3_eq, comparator_3_gt, comparator_4_eq, DYN_out, gtr_out,
       JMP_out, LB_out, LLI_out, LNI_LI_out, NAND_out, not_1_out, not_2_out, or_1_out, or_2_out, or_4_out,
       OR_5_out, or_6_out, or_8_out, or_11_out, or_12_out, or_13_out, or_14_out, or_15_out, or_16_out,
       or_17_out, or_18_out, or_19_out, or_20_out, or_21_out, or_22_out, or_23_out, or_24_out, or_25_out,
       or_26_out, or_27_out, or_28_out, or_29_out, or_30_out, or_31_out, or_32_out, or_34_out, or_35_out,
       or_36_out, or_37_out, or_40_out, or_42_out, or_43_out, or_46_out, or_49_out, or_50_out, or_52_out,
       or_53_out, or_55_out, or_56_out, or_57_out, or_58_out, PEEK_out, POP_out, ptrinc_out, PUSH_out,
       register_3_q, register_4_q, register_5_q, register_6_q, register_9_q, SOP_out, SP_out;
  wire [1:0] multiplexer_1_out, multiplexer_3_out, multiplexer_4_out, multiplexer_5_out, multiplexer_8_out,
       multiplexer_9_out, multiplexer_10_out, multiplexer_11_out, multiplexer_12_out, multiplexer_13_out,
       multiplexer_14_out, multiplexer_15_out, multiplexer_16_out, multiplexer_17_out, multiplexer_18_out,
       multiplexer_19_out, multiplexer_20_out, multiplexer_21_out, multiplexer_22_out, multiplexer_23_out,
       multiplexer_24_out, multiplexer_25_out, multiplexer_26_out;
  wire [3:0] multiplexer_1_out_3;
  wire [3:2] multiplexer_1_out_2;
  wire [4:0] adder_2_out, bit_extender_1_out, multiplexer_27_out, register_7_q, subtractor_1_out;
  wire [7:0] adder_1_out, multiplexer_2_out, multiplexer_6_out, or_3_out, register_1_q;

  not not_1 (not_1_out, or_58_out);
  Register #(.trigger("falling")) register_1 (.D(DATA), .en(not_1_out), .Q(register_1_q), .clk(CLK), .clr(RST));
  Multiplexer #(.width(8), .enable("false")) multiplexer_1 (
    .in0(register_1_q), .in1({8{1'b0}}), .out({multiplexer_1_out_2, multiplexer_1_out_3, multiplexer_1_out}),
    .sel(or_49_out));
  Multiplexer #(.width(8), .enable("false")) multiplexer_2 (
    .in0(ALU_OUTPUT), .in1(adder_1_out), .out(multiplexer_2_out), .sel(ptrinc_out));
  Adder adder_1 (.a(8'h1), .b(MEM_POINTER), .out(adder_1_out));  // open: cin, cout
  or or_1 (or_1_out, multiplexer_1_out_3[0], multiplexer_1_out_3[1]);
  or or_2 (or_2_out, multiplexer_1_out_3[0], multiplexer_1_out_3[1]);
  and and_1 (and_1_out, ~multiplexer_1_out_3[2], ~multiplexer_1_out_3[3]);  // AND_Gate
  Multiplexer #(.width(2), .enable("false")) multiplexer_3 (
    .in0(2'b00), .in1(multiplexer_1_out_3[1:0]), .out(multiplexer_3_out), .sel(or_22_out));
  Multiplexer #(.width(2), .enable("false")) multiplexer_4 (
    .in0(2'b00), .in1(multiplexer_1_out_3[3:2]), .out(multiplexer_4_out), .sel(or_23_out));
  Multiplexer #(.width(2), .enable("false")) multiplexer_5 (
    .in0(2'b00), .in1(multiplexer_1_out_2), .out(multiplexer_5_out), .sel(or_27_out));
  assign or_3_out = {multiplexer_1_out_3, 4'b0000} | ALU_OUTPUT;  // OR_Gate or_3, 8 bits wide
  Register register_2 (.D(multiplexer_2_out), .en(or_4_out), .Q(MEM_POINTER), .clk(CLK), .clr(RST));
  or or_4 (or_4_out, SP_out, ptrinc_out);
  and OR_5 (OR_5_out, ~multiplexer_1_out[0], ~multiplexer_1_out[1], 1'b1, or_1_out, 1'b1, 1'b1, 1'b1, 1'b1);  // AND_Gate
  and SOP (SOP_out, ~multiplexer_1_out[0], ~multiplexer_1_out[1], ~multiplexer_1_out_3[0], ~multiplexer_1_out_3[1], 1'b1, 1'b1, 1'b1, 1'b1);  // AND_Gate
  and NAND (NAND_out, multiplexer_1_out[0], ~multiplexer_1_out[1], 1'b1, 1'b1, 1'b1, 1'b1, 1'b1, 1'b1);  // AND_Gate
  or or_6 (or_6_out, NAND_out, 1'b0);
  and DYN (DYN_out, ~multiplexer_1_out[0], multiplexer_1_out[1], 1'b1, or_2_out, 1'b1, 1'b1, 1'b1, 1'b1);  // AND_Gate
  and CIN (CIN_out, ~multiplexer_1_out[0], multiplexer_1_out[1], ~multiplexer_1_out_3[0], ~multiplexer_1_out_3[1], 1'b1, 1'b1, 1'b1, 1'b1);  // AND_Gate
  or or_7 (ALU_OP[2], CIN_out, or_6_out);
  and LLI (LLI_out, multiplexer_1_out[0], multiplexer_1_out[1], 1'b1, 1'b1, 1'b1, 1'b1, ~multiplexer_1_out_2[2], ~multiplexer_1_out_2[3]);  // AND_Gate
  and LNI_LI (LNI_LI_out, multiplexer_1_out[0], multiplexer_1_out[1], 1'b1, 1'b1, 1'b1, 1'b1, multiplexer_1_out_2[2], ~multiplexer_1_out_2[3]);  // AND_Gate
  and JMP (JMP_out, multiplexer_1_out[0], multiplexer_1_out[1], ~multiplexer_1_out_3[0], ~multiplexer_1_out_3[1], ~multiplexer_1_out_3[2], ~multiplexer_1_out_3[3], ~multiplexer_1_out_2[2], multiplexer_1_out_2[3]);  // AND_Gate
  and u_PUSH (PUSH_out, multiplexer_1_out[0], multiplexer_1_out[1], ~multiplexer_1_out_3[0], ~multiplexer_1_out_3[1], multiplexer_1_out_3[2], ~multiplexer_1_out_3[3], ~multiplexer_1_out_2[2], multiplexer_1_out_2[3]);  // AND_Gate
  and u_POP (POP_out, multiplexer_1_out[0], multiplexer_1_out[1], ~multiplexer_1_out_3[0], ~multiplexer_1_out_3[1], ~multiplexer_1_out_3[2], multiplexer_1_out_3[3], ~multiplexer_1_out_2[2], multiplexer_1_out_2[3]);  // AND_Gate
  and PEEK (PEEK_out, multiplexer_1_out[0], multiplexer_1_out[1], ~multiplexer_1_out_3[0], ~multiplexer_1_out_3[1], multiplexer_1_out_3[2], multiplexer_1_out_3[3], ~multiplexer_1_out_2[2], multiplexer_1_out_2[3]);  // AND_Gate
  and and_2 (and_2_out, and_1_out, LB_out);
  and LB (LB_out, multiplexer_1_out[0], multiplexer_1_out[1], multiplexer_1_out_3[0], ~multiplexer_1_out_3[1], 1'b1, 1'b1, ~multiplexer_1_out_2[2], multiplexer_1_out_2[3]);  // AND_Gate
  and and_3 (and_3_out, and_1_out, Write_Enable);
  and SB (Write_Enable, multiplexer_1_out[0], multiplexer_1_out[1], ~multiplexer_1_out_3[0], multiplexer_1_out_3[1], 1'b1, 1'b1, ~multiplexer_1_out_2[2], multiplexer_1_out_2[3]);  // AND_Gate
  and and_4 (and_4_out, and_1_out, SP_out);
  and SP (SP_out, multiplexer_1_out[0], multiplexer_1_out[1], multiplexer_1_out_3[0], multiplexer_1_out_3[1], 1'b1, 1'b1, ~multiplexer_1_out_2[2], multiplexer_1_out_2[3]);  // AND_Gate
  and CMP (CMP_out, multiplexer_1_out[0], multiplexer_1_out[1], 1'b1, 1'b1, 1'b1, 1'b1, multiplexer_1_out_2[2], multiplexer_1_out_2[3]);
  Multiplexer #(.width(8), .enable("false")) multiplexer_6 (
    .in0(or_3_out), .in1({4'b0000, multiplexer_1_out_3}), .out(multiplexer_6_out), .sel(LLI_out));
  or or_8 (or_8_out, NAND_out, 1'b0);
  or or_9 (ALU_OP[1], DYN_out, 1'b0);
  or or_10 (ALU_OP[0], DYN_out, or_8_out);
  Comparator #(.mode("unsigned")) comparator_1 (.a(MEM_POINTER), .b(8'hfc), .lt(comparator_1_lt));  // open: gt, eq
  and and_5 (Memory_Select, comparator_1_lt, Address_MUX);
  or or_11 (or_11_out, OR_5_out, 1'b0);
  or or_12 (or_12_out, OR_5_out, 1'b0);
  or or_13 (or_13_out, NAND_out, or_12_out);
  or or_14 (or_14_out, NAND_out, or_11_out);
  or or_15 (or_15_out, DYN_out, or_13_out);
  or or_16 (or_16_out, DYN_out, or_14_out);
  or or_17 (or_17_out, CIN_out, or_15_out);
  or or_18 (or_18_out, CIN_out, or_16_out);
  or or_19 (or_19_out, LB_out, or_17_out);
  or or_20 (or_20_out, Write_Enable, or_19_out);
  or or_21 (or_21_out, SP_out, or_20_out);
  or or_22 (or_22_out, CMP_out, or_18_out);
  or or_23 (or_23_out, CMP_out, or_21_out);
  Multiplexer #(.width(8), .enable("false")) multiplexer_7 (
    .in0(multiplexer_6_out), .in1(PC_ADDRESS), .out(IMM_VALUE), .sel(gtr_out));
  or or_24 (or_24_out, OR_5_out, 1'b0);
  or or_25 (or_25_out, NAND_out, or_24_out);
  or or_26 (or_26_out, DYN_out, or_25_out);
  or or_27 (or_27_out, CIN_out, or_26_out);
  or or_28 (or_28_out, LLI_out, 1'b0);
  or or_29 (or_29_out, POP_out, or_28_out);
  or or_30 (or_30_out, PEEK_out, or_29_out);
  or or_31 (or_31_out, and_3_out, or_30_out);
  or or_32 (or_32_out, and_4_out, or_31_out);
  or or_33 (GPR_MUX[1], gtr_out, or_32_out);
  or or_34 (or_34_out, LLI_out, 1'b0);
  or or_35 (or_35_out, LNI_LI_out, or_34_out, or_55_out);
  or or_36 (or_36_out, LB_out, 1'b0);
  or or_37 (or_37_out, LB_out, or_35_out);
  or or_38 (Address_MUX, Write_Enable, or_36_out);
  or or_39 (GPR_MUX[0], gtr_out, or_37_out);
  Register #(.width(1), .trigger("falling")) register_3 (
    .D(and_6_out), .Q(register_3_q), .clk(CLK), .clr(RST));  // open: en
  and and_6 (and_6_out, JMP_FLAG, CMP_out);
  or or_40 (or_40_out, and_3_out, POP_out);
  or or_41 (POP, and_4_out, or_40_out);
  and and_7 (BRANCH[0], JMP_out, ~register_3_q);  // AND_Gate
  Multiplexer #(.width(2), .enable("false")) multiplexer_8 (
    .in0(2'b00), .in1(2'b00), .out(multiplexer_8_out), .sel(LLI_out));
  and and_8 (and_8_out, LNI_LI_out, and_11_out);
  Multiplexer #(.width(2), .disabled(0), .enable("false")) multiplexer_9 (
    .in0(multiplexer_8_out), .in1(2'b00), .out(multiplexer_9_out), .sel(and_8_out));
  Multiplexer #(.width(2), .disabled(0), .enable("false")) multiplexer_10 (
    .in0(multiplexer_9_out), .in1(2'b01), .out(multiplexer_10_out), .sel(BRANCH[1]));
  Multiplexer #(.width(2), .enable("false")) multiplexer_11 (
    .in0(multiplexer_10_out), .in1(2'b01), .out(multiplexer_11_out), .sel(PUSH_out));
  and and_9 (and_9_out, ~and_11_out, or_55_out);  // AND_Gate
  or or_42 (or_42_out, PUSH_out, and_9_out);
  Multiplexer #(.width(2), .enable("false")) multiplexer_12 (
    .in0(multiplexer_11_out), .in1(2'b00), .out(multiplexer_12_out), .sel(POP_out));
  Multiplexer #(.width(2), .enable("false")) multiplexer_13 (
    .in0(multiplexer_12_out), .in1(2'b00), .out(multiplexer_13_out), .sel(PEEK_out));
  or or_43 (or_43_out, and_2_out, or_42_out);
  or or_44 (PUSH, gtr_out, or_43_out);
  assign A__R = multiplexer_3_out | multiplexer_13_out;  // OR_Gate or_45, 2 bits wide
  Register #(.width(1), .trigger("falling")) register_4 (
    .D(or_46_out), .Q(register_4_q), .clk(CLK), .clr(RST));  // open: en
  or or_46 (or_46_out, JMP_out, Address_MUX);
  and and_10 (External_Address_Select, ~comparator_1_lt, Address_MUX);  // AND_Gate
  Multiplexer #(.width(2), .enable("false")) multiplexer_14 (
    .in0(2'b00), .in1(2'b00), .out(multiplexer_14_out), .sel(LLI_out));
  Multiplexer #(.width(2), .enable("false")) multiplexer_15 (
    .in0(2'b00), .in1(2'b01), .out(multiplexer_15_out), .sel(LLI_out));
  Multiplexer #(.width(2), .disabled(0), .enable("false")) multiplexer_16 (
    .in0(multiplexer_15_out), .in1(2'b01), .out(multiplexer_16_out), .sel(and_8_out));
  Multiplexer #(.width(2), .disabled(0), .enable("false")) multiplexer_17 (
    .in0(multiplexer_14_out), .in1(2'b00), .out(multiplexer_17_out), .sel(and_8_out));
  Multiplexer #(.width(2), .disabled(0), .enable("false")) multiplexer_18 (
    .in0(multiplexer_16_out), .in1(2'b00), .out(multiplexer_18_out), .sel(BRANCH[1]));
  Multiplexer #(.width(2), .disabled(0), .enable("false")) multiplexer_19 (
    .in0(multiplexer_17_out), .in1(2'b00), .out(multiplexer_19_out), .sel(BRANCH[1]));
  Multiplexer #(.width(2), .enable("false")) multiplexer_20 (
    .in0(multiplexer_18_out), .in1(2'b00), .out(multiplexer_20_out), .sel(PUSH_out));
  Multiplexer #(.width(2), .enable("false")) multiplexer_21 (
    .in0(multiplexer_19_out), .in1(2'b00), .out(multiplexer_21_out), .sel(PUSH_out));
  Multiplexer #(.width(2), .enable("false")) multiplexer_22 (
    .in0(multiplexer_21_out), .in1(2'b00), .out(multiplexer_22_out), .sel(POP_out));
  Multiplexer #(.width(2), .enable("false")) multiplexer_23 (
    .in0(multiplexer_20_out), .in1(2'b01), .out(multiplexer_23_out), .sel(POP_out));
  Multiplexer #(.width(2), .enable("false")) multiplexer_24 (
    .in0(multiplexer_22_out), .in1(2'b00), .out(multiplexer_24_out), .sel(PEEK_out));
  Multiplexer #(.width(2), .enable("false")) multiplexer_25 (
    .in0(multiplexer_23_out), .in1(2'b01), .out(multiplexer_25_out), .sel(PEEK_out));
  Multiplexer #(.width(2), .enable("false")) multiplexer_26 (
    .in0(multiplexer_5_out), .in1(multiplexer_4_out), .out(multiplexer_26_out), .sel(Address_MUX));
  assign B__R = multiplexer_4_out | multiplexer_24_out;  // OR_Gate or_47, 2 bits wide
  assign C__W = multiplexer_26_out | multiplexer_25_out;  // OR_Gate or_48, 2 bits wide
  or or_49 (or_49_out, register_4_q, or_58_out);
  Register #(.width(1)) register_5 (.D(LNI_LI_out), .Q(register_5_q), .clk(CLK), .clr(RST));  // open: en
  and and_11 (and_11_out, comparator_3_eq, LNI_LI_out);
  Register #(.width(1)) register_6 (.D(and_11_out), .Q(register_6_q), .clk(CLK), .clr(RST));  // open: en
  or or_50 (or_50_out, and_2_out, and_3_out, and_4_out);
  or or_51 (ALU_State, DYN_out, CMP_out);
  and gtr (gtr_out, ~multiplexer_1_out_3[2], multiplexer_1_out_3[3], ~multiplexer_1_out_2[2], multiplexer_1_out_2[3], SOP_out);  // AND_Gate
  and go (BRANCH[1], multiplexer_1_out_3[2], ~multiplexer_1_out_3[3], ~multiplexer_1_out_2[2], multiplexer_1_out_2[3], SOP_out);  // AND_Gate
  and ptrinc (ptrinc_out, multiplexer_1_out_3[2], multiplexer_1_out_3[3], multiplexer_1_out_2[2], multiplexer_1_out_2[3], SOP_out);
  or or_52 (or_52_out, gtr_out, ptrinc_out, BRANCH[1]);
  Multiplexer #(.width(5), .enable("false")) multiplexer_27 (
    .in0(subtractor_1_out), .in1(adder_2_out), .out(multiplexer_27_out), .sel(LNI_LI_out));
  or or_53 (or_53_out, and_12_out, and_14_out);
  and and_12 (and_12_out, register_5_q, CLK);
  or or_54 (GPR_Forward_Input, or_55_out, or_50_out, gtr_out);
  and and_13 (and_13_out, SOP_out, ~or_55_out, ~or_52_out, ~or_49_out);  // AND_Gate
  Comparator #(.width(5)) comparator_2 (
    .a(multiplexer_27_out), .b({5{1'b0}}), .gt(comparator_2_gt), .eq(comparator_2_eq));  // open: lt
  Register #(.width(5)) register_7 (.D(multiplexer_27_out), .Q(register_7_q), .clk(or_53_out), .clr(RST));  // open: en
  and and_14 (and_14_out, CLK, not_2_out);
  and and_15 (and_15_out, not_2_out, ~register_6_q);  // AND_Gate
  or or_55 (or_55_out, LNI_LI_out, and_15_out);
  Comparator #(.width(4)) comparator_3 (
    .a(multiplexer_1_out_3), .b(4'b0000), .gt(comparator_3_gt), .eq(comparator_3_eq));  // open: lt
  Adder #(.width(5)) adder_2 (
    .a({5{1'b0}}), .b(bit_extender_1_out), .out(adder_2_out), .cin(comparator_3_eq));  // open: cout
  assign bit_extender_1_out = {{1{1'b0}}, multiplexer_1_out_3};  // Bit_Extender bit_extender_1
  Register #(.width(4), .trigger("falling")) register_8 (
    .D({multiplexer_1_out_2, multiplexer_1_out_3[3:2]}), .en(and_13_out), .Q(Dynamic_OP), .clk(CLK), .clr(RST));
  or or_56 (or_56_out, comparator_2_gt, comparator_2_eq);
  and and_16 (and_16_out, or_56_out, ~and_11_out);  // AND_Gate
  Subtractor #(.width(5)) subtractor_1 (.a(register_7_q), .b(5'b00001), .out(subtractor_1_out));  // open: bin, bout
  or or_57 (or_57_out, not_2_out, comparator_3_gt);
  not not_2 (not_2_out, comparator_4_eq);
  Comparator #(.width(5)) comparator_4 (.a(register_7_q), .b({5{1'b0}}), .eq(comparator_4_eq));  // open: gt, lt
  and and_17 (and_17_out, and_16_out, or_57_out, ~register_6_q);  // AND_Gate
  Register #(.width(1)) register_9 (.D(and_17_out), .Q(register_9_q), .clk(CLK), .clr(RST));  // open: en
  or or_58 (or_58_out, not_2_out, register_9_q);

  // Notes on the sheet:
  //   This input defines the range of MMIO -->
endmodule

module STK (
  input  [7:0] in_1,
  input  in_2,
  input  in_3,
  input  in_4,
  input  in_5,
  output [7:0] out_6
);

  wire or_1_out;
  wire [7:0] multiplexer_1_out, multiplexer_2_out, multiplexer_3_out, multiplexer_4_out, multiplexer_5_out,
       multiplexer_6_out, multiplexer_7_out, multiplexer_8_out, multiplexer_9_out, multiplexer_10_out,
       multiplexer_11_out, multiplexer_12_out, multiplexer_13_out, multiplexer_14_out, multiplexer_15_out,
       multiplexer_16_out, multiplexer_17_out, multiplexer_18_out, multiplexer_19_out, multiplexer_20_out,
       multiplexer_21_out, multiplexer_22_out, multiplexer_23_out, multiplexer_24_out, multiplexer_25_out,
       multiplexer_26_out, multiplexer_27_out, multiplexer_28_out, multiplexer_29_out, multiplexer_30_out,
       multiplexer_31_out, multiplexer_32_out, register_2_q, register_3_q, register_4_q, register_5_q,
       register_6_q, register_7_q, register_8_q, register_9_q, register_10_q, register_11_q, register_12_q,
       register_13_q, register_14_q, register_15_q, register_16_q, register_17_q, register_18_q,
       register_19_q, register_20_q, register_21_q, register_22_q, register_23_q, register_24_q,
       register_25_q, register_26_q, register_27_q, register_28_q, register_29_q, register_30_q,
       register_31_q, register_32_q;

  or or_1 (or_1_out, in_4, in_5);
  Multiplexer #(.width(8), .enable("false")) multiplexer_1 (
    .in0(register_2_q), .in1(in_1), .out(multiplexer_1_out), .sel(in_5));
  Multiplexer #(.width(8), .enable("false")) multiplexer_2 (
    .in0(register_3_q), .in1(out_6), .out(multiplexer_2_out), .sel(in_5));
  Register register_1 (.D(multiplexer_1_out), .en(or_1_out), .Q(out_6), .clk(in_2), .clr(in_3));
  Register register_2 (.D(multiplexer_2_out), .en(or_1_out), .Q(register_2_q), .clk(in_2), .clr(in_3));
  Multiplexer #(.width(8), .enable("false")) multiplexer_3 (
    .in0(register_4_q), .in1(register_2_q), .out(multiplexer_3_out), .sel(in_5));
  Register register_3 (.D(multiplexer_3_out), .en(or_1_out), .Q(register_3_q), .clk(in_2), .clr(in_3));
  Multiplexer #(.width(8), .enable("false")) multiplexer_4 (
    .in0(register_5_q), .in1(register_3_q), .out(multiplexer_4_out), .sel(in_5));
  Register register_4 (.D(multiplexer_4_out), .en(or_1_out), .Q(register_4_q), .clk(in_2), .clr(in_3));
  Multiplexer #(.width(8), .enable("false")) multiplexer_5 (
    .in0(register_6_q), .in1(register_4_q), .out(multiplexer_5_out), .sel(in_5));
  Register register_5 (.D(multiplexer_5_out), .en(or_1_out), .Q(register_5_q), .clk(in_2), .clr(in_3));
  Multiplexer #(.width(8), .enable("false")) multiplexer_6 (
    .in0(register_7_q), .in1(register_5_q), .out(multiplexer_6_out), .sel(in_5));
  Multiplexer #(.width(8), .enable("false")) multiplexer_7 (
    .in0(register_8_q), .in1(register_6_q), .out(multiplexer_7_out), .sel(in_5));
  Register register_6 (.D(multiplexer_6_out), .en(or_1_out), .Q(register_6_q), .clk(in_2), .clr(in_3));
  Register register_7 (.D(multiplexer_7_out), .en(or_1_out), .Q(register_7_q), .clk(in_2), .clr(in_3));
  Multiplexer #(.width(8), .enable("false")) multiplexer_8 (
    .in0(register_9_q), .in1(register_7_q), .out(multiplexer_8_out), .sel(in_5));
  Register register_8 (.D(multiplexer_8_out), .en(or_1_out), .Q(register_8_q), .clk(in_2), .clr(in_3));
  Multiplexer #(.width(8), .enable("false")) multiplexer_9 (
    .in0(register_10_q), .in1(register_8_q), .out(multiplexer_9_out), .sel(in_5));
  Multiplexer #(.width(8), .enable("false")) multiplexer_10 (
    .in0(register_11_q), .in1(register_9_q), .out(multiplexer_10_out), .sel(in_5));
  Register register_9 (.D(multiplexer_9_out), .en(or_1_out), .Q(register_9_q), .clk(in_2), .clr(in_3));
  Register register_10 (.D(multiplexer_10_out), .en(or_1_out), .Q(register_10_q), .clk(in_2), .clr(in_3));
  Multiplexer #(.width(8), .enable("false")) multiplexer_11 (
    .in0(register_12_q), .in1(register_10_q), .out(multiplexer_11_out), .sel(in_5));
  Register register_11 (.D(multiplexer_11_out), .en(or_1_out), .Q(register_11_q), .clk(in_2), .clr(in_3));
  Multiplexer #(.width(8), .enable("false")) multiplexer_12 (
    .in0(register_13_q), .in1(register_11_q), .out(multiplexer_12_out), .sel(in_5));
  Register register_12 (.D(multiplexer_12_out), .en(or_1_out), .Q(register_12_q), .clk(in_2), .clr(in_3));
  Multiplexer #(.width(8), .enable("false")) multiplexer_13 (
    .in0(register_14_q), .in1(register_12_q), .out(multiplexer_13_out), .sel(in_5));
  Register register_13 (.D(multiplexer_13_out), .en(or_1_out), .Q(register_13_q), .clk(in_2), .clr(in_3));
  Multiplexer #(.width(8), .enable("false")) multiplexer_14 (
    .in0(register_15_q), .in1(register_13_q), .out(multiplexer_14_out), .sel(in_5));
  Multiplexer #(.width(8), .enable("false")) multiplexer_15 (
    .in0(register_16_q), .in1(register_14_q), .out(multiplexer_15_out), .sel(in_5));
  Register register_14 (.D(multiplexer_14_out), .en(or_1_out), .Q(register_14_q), .clk(in_2), .clr(in_3));
  Register register_15 (.D(multiplexer_15_out), .en(or_1_out), .Q(register_15_q), .clk(in_2), .clr(in_3));
  Multiplexer #(.width(8), .enable("false")) multiplexer_16 (
    .in0(register_17_q), .in1(register_15_q), .out(multiplexer_16_out), .sel(in_5));
  Register register_16 (.D(multiplexer_16_out), .en(or_1_out), .Q(register_16_q), .clk(in_2), .clr(in_3));
  Multiplexer #(.width(8), .enable("false")) multiplexer_17 (
    .in0(register_18_q), .in1(register_16_q), .out(multiplexer_17_out), .sel(in_5));
  Multiplexer #(.width(8), .enable("false")) multiplexer_18 (
    .in0(register_19_q), .in1(register_17_q), .out(multiplexer_18_out), .sel(in_5));
  Register register_17 (.D(multiplexer_17_out), .en(or_1_out), .Q(register_17_q), .clk(in_2), .clr(in_3));
  Register register_18 (.D(multiplexer_18_out), .en(or_1_out), .Q(register_18_q), .clk(in_2), .clr(in_3));
  Multiplexer #(.width(8), .enable("false")) multiplexer_19 (
    .in0(register_20_q), .in1(register_18_q), .out(multiplexer_19_out), .sel(in_5));
  Register register_19 (.D(multiplexer_19_out), .en(or_1_out), .Q(register_19_q), .clk(in_2), .clr(in_3));
  Multiplexer #(.width(8), .enable("false")) multiplexer_20 (
    .in0(register_21_q), .in1(register_19_q), .out(multiplexer_20_out), .sel(in_5));
  Register register_20 (.D(multiplexer_20_out), .en(or_1_out), .Q(register_20_q), .clk(in_2), .clr(in_3));
  Multiplexer #(.width(8), .enable("false")) multiplexer_21 (
    .in0(register_22_q), .in1(register_20_q), .out(multiplexer_21_out), .sel(in_5));
  Register register_21 (.D(multiplexer_21_out), .en(or_1_out), .Q(register_21_q), .clk(in_2), .clr(in_3));
  Multiplexer #(.width(8), .enable("false")) multiplexer_22 (
    .in0(register_23_q), .in1(register_21_q), .out(multiplexer_22_out), .sel(in_5));
  Multiplexer #(.width(8), .enable("false")) multiplexer_23 (
    .in0(register_24_q), .in1(register_22_q), .out(multiplexer_23_out), .sel(in_5));
  Register register_22 (.D(multiplexer_22_out), .en(or_1_out), .Q(register_22_q), .clk(in_2), .clr(in_3));
  Register register_23 (.D(multiplexer_23_out), .en(or_1_out), .Q(register_23_q), .clk(in_2), .clr(in_3));
  Multiplexer #(.width(8), .enable("false")) multiplexer_24 (
    .in0(register_25_q), .in1(register_23_q), .out(multiplexer_24_out), .sel(in_5));
  Register register_24 (.D(multiplexer_24_out), .en(or_1_out), .Q(register_24_q), .clk(in_2), .clr(in_3));
  Multiplexer #(.width(8), .enable("false")) multiplexer_25 (
    .in0(register_26_q), .in1(register_24_q), .out(multiplexer_25_out), .sel(in_5));
  Multiplexer #(.width(8), .enable("false")) multiplexer_26 (
    .in0(register_27_q), .in1(register_25_q), .out(multiplexer_26_out), .sel(in_5));
  Register register_25 (.D(multiplexer_25_out), .en(or_1_out), .Q(register_25_q), .clk(in_2), .clr(in_3));
  Register register_26 (.D(multiplexer_26_out), .en(or_1_out), .Q(register_26_q), .clk(in_2), .clr(in_3));
  Multiplexer #(.width(8), .enable("false")) multiplexer_27 (
    .in0(register_28_q), .in1(register_26_q), .out(multiplexer_27_out), .sel(in_5));
  Register register_27 (.D(multiplexer_27_out), .en(or_1_out), .Q(register_27_q), .clk(in_2), .clr(in_3));
  Multiplexer #(.width(8), .enable("false")) multiplexer_28 (
    .in0(register_29_q), .in1(register_27_q), .out(multiplexer_28_out), .sel(in_5));
  Register register_28 (.D(multiplexer_28_out), .en(or_1_out), .Q(register_28_q), .clk(in_2), .clr(in_3));
  Multiplexer #(.width(8), .enable("false")) multiplexer_29 (
    .in0(register_30_q), .in1(register_28_q), .out(multiplexer_29_out), .sel(in_5));
  Register register_29 (.D(multiplexer_29_out), .en(or_1_out), .Q(register_29_q), .clk(in_2), .clr(in_3));
  Multiplexer #(.width(8), .enable("false")) multiplexer_30 (
    .in0(register_31_q), .in1(register_29_q), .out(multiplexer_30_out), .sel(in_5));
  Multiplexer #(.width(8), .enable("false")) multiplexer_31 (
    .in0(register_32_q), .in1(register_30_q), .out(multiplexer_31_out), .sel(in_5));
  Register register_30 (.D(multiplexer_30_out), .en(or_1_out), .Q(register_30_q), .clk(in_2), .clr(in_3));
  Register register_31 (.D(multiplexer_31_out), .en(or_1_out), .Q(register_31_q), .clk(in_2), .clr(in_3));
  Multiplexer #(.width(8), .enable("false")) multiplexer_32 (
    .in0({8{1'b0}}), .in1(register_31_q), .out(multiplexer_32_out), .sel(in_5));
  Register register_32 (.D(multiplexer_32_out), .en(or_1_out), .Q(register_32_q), .clk(in_2), .clr(in_3));
endmodule

module PC (
  input  [7:0] DATA,
  input  [7:0] ALU,
  input  [1:0] Jump_Enable,
  input  in_4,
  input  in_5,
  input  in_6,
  output [7:0] out_7,
  output [7:0] out_8
);

  wire not_1_out;
  wire [7:0] adder_1_out, adder_2_out, multiplexer_1_out, register_1_q;

  Adder adder_1 (.a(ALU), .b(8'h1), .out(adder_1_out));  // open: cin, cout
  Multiplexer #(.select(2), .width(8), .enable("false")) multiplexer_1 (
    .in0(adder_2_out), .in1(DATA), .in2(adder_1_out), .out(multiplexer_1_out), .sel(Jump_Enable));  // open: in3
  Register #(.trigger("falling")) register_1 (
    .D(multiplexer_1_out), .en(not_1_out), .Q(register_1_q), .clk(in_5), .clr(in_6));
  not not_1 (not_1_out, in_4);
  Adder adder_2 (.a(register_1_q), .b(8'h1), .out(adder_2_out));  // open: cin, cout
  Multiplexer #(.width(8), .disabled(0), .enable("false")) multiplexer_2 (
    .in0(register_1_q), .in1(ALU), .out(out_8), .sel(Jump_Enable[1]));
  Adder adder_3 (.a(adder_2_out), .b(8'h1), .out(out_7));  // open: cin, cout
endmodule

module ExampleConfigurationROM (
  input  [7:0] in_1,
  input  [7:0] in_2,
  input  RESET,
  output WRITE_ACTIVE,
  output IO_ACTIVE,
  output IO_ENABLE
);

  wire and_1_out, and_2_out, and_3_out, and_4_out, and_5_out, and_6_out, and_7_out, and_8_out, and_9_out,
       and_10_out, CLOCK_out, comparator_1_gt, comparator_2_eq, comparator_3_eq, comparator_4_eq,
       comparator_5_eq, keyboard_1_avail, or_2_out, or_3_out;
  wire [7:0] controlled_buffer_1_out, keyboard_1_data, mcu_1_addr, mcu_1_out, register_1_q, register_2_q,
       register_3_q, rom_1_data;

  MCU mcu_1 (
    .IO_ENABLE(IO_ENABLE), .IN(controlled_buffer_1_out), .ADDR(mcu_1_addr), .OUT(mcu_1_out), .CLK(CLOCK_out),
    .RST(RESET), .IO_ACTIVE(IO_ACTIVE), .WRITE_ACTIVE(WRITE_ACTIVE));
  or or_1 (IO_ENABLE, or_2_out, and_1_out);
  or or_2 (or_2_out, or_3_out, and_3_out);
  or or_3 (or_3_out, and_5_out, and_4_out);
  Clock CLOCK (.out(CLOCK_out));
  Comparator #(.mode("unsigned")) comparator_1 (.a(8'hfc), .b(mcu_1_addr), .gt(comparator_1_gt));  // open: eq, lt
  Comparator #(.mode("unsigned")) comparator_2 (.a(mcu_1_addr), .b({8{1'b1}}), .eq(comparator_2_eq));  // open: gt, lt
  Comparator #(.mode("unsigned")) comparator_3 (.a(mcu_1_addr), .b(8'hfe), .eq(comparator_3_eq));  // open: gt, lt
  Comparator #(.mode("unsigned")) comparator_4 (.a(mcu_1_addr), .b(8'hfd), .eq(comparator_4_eq));  // open: gt, lt
  Comparator #(.mode("unsigned")) comparator_5 (.a(mcu_1_addr), .b(8'hfc), .eq(comparator_5_eq));  // open: gt, lt
  // Probe on controlled_buffer_1_out
  // Probe on mcu_1_addr
  // Probe on mcu_1_out
  and and_1 (and_1_out, comparator_1_gt, ~IO_ACTIVE);  // AND_Gate
  and and_2 (and_2_out, IO_ACTIVE, comparator_2_eq, WRITE_ACTIVE);
  and and_3 (and_3_out, comparator_3_eq, IO_ACTIVE);
  and and_4 (and_4_out, comparator_4_eq, IO_ACTIVE);
  and and_5 (and_5_out, comparator_5_eq, IO_ACTIVE);
  Register register_1 (.D(mcu_1_out), .en(and_2_out), .Q(register_1_q), .clk(CLOCK_out), .clr(RESET));
  // Probe on {register_1_q, mcu_1_addr}
  Register register_2 (.D(mcu_1_out), .en(and_6_out), .Q(register_2_q), .clk(CLOCK_out), .clr(RESET));
  and and_6 (and_6_out, and_3_out, WRITE_ACTIVE);
  Hex_Digit_Display hex_digit_display_1 (.value(register_2_q[7:4]));  // open: dp
  Register register_3 (.D(mcu_1_out), .en(and_7_out), .Q(register_3_q), .clk(CLOCK_out), .clr(RESET));
  and and_7 (and_7_out, and_4_out, WRITE_ACTIVE);
  Hex_Digit_Display hex_digit_display_2 (.value(register_3_q[7:4]));  // open: dp
  and and_8 (and_8_out, ~mcu_1_out[7], WRITE_ACTIVE);  // AND_Gate
  and and_9 (and_9_out, mcu_1_out[7], WRITE_ACTIVE);
  and and_10 (and_10_out, and_5_out, CLOCK_out);
  Hex_Digit_Display hex_digit_display_3 (.value(register_2_q[3:0]));  // open: dp
  Hex_Digit_Display hex_digit_display_4 (.value(register_3_q[3:0]));  // open: dp
  TTY #(.cols(80)) tty_1 (.data(mcu_1_out[6:0]), .clk(and_10_out), .we(and_8_out), .clr(RESET));
  Keyboard #(.buflen(80), .trigger("falling")) keyboard_1 (
    .clk(and_10_out), .re(and_9_out), .clr(RESET), .avail(keyboard_1_avail), .data(keyboard_1_data[6:0]));
  ROM #(.addrWidth(16)) rom_1 (.addr({register_1_q, mcu_1_addr}), .data(rom_1_data));  // open: sel
  assign controlled_buffer_1_out = and_1_out ? rom_1_data : 8'bz;  // Controlled_Buffer controlled_buffer_1
  assign controlled_buffer_1_out = and_3_out ? in_1 : 8'bz;  // Controlled_Buffer controlled_buffer_2
  assign controlled_buffer_1_out = and_4_out ? in_2 : 8'bz;  // Controlled_Buffer controlled_buffer_3
  not not_1 (keyboard_1_data[7], keyboard_1_avail);
  assign controlled_buffer_1_out = and_5_out ? keyboard_1_data : 8'bz;  // Controlled_Buffer controlled_buffer_4

  // Notes on the sheet:
  //   Sets the memory-mapped address range
  //   Memory Mapped I/O Port Address
  //   Memory Mapped I/O Port Address
  //   Memory Mapped I/O Port Address
  //   PROGRAM MEMORY
  //   Output:
  //   contents of rom_1 (hex, n*v repeats v):
  //   67 0 a 21 65 6d 6f 63 6c 65 57 a0 83 e4 4b 0 20 24 a0 83 e4 43 20 c4 30 47 80 fc 8f a3 a7 db 83 1e
  //   9b 23 e7 83 36 ab bf ab f2 43 6e f7 83 e 2b db 83 41 83 18 43 20 f7 83 18 ab 7 10 de 83 18 43 20 93
  //   10 de 7 9f bb f0 8b 5b 0 a 67 6e 69 70 5 a0 83 bf 20 eb 83 66 57 0 a 67 6e 6f 70 a0 83 e4 83 e 73 0
  //   a 33 32 31 67 6e 69 74 73 65 74 b a0 83 bf 20 eb 83 8f 77 0 a 65 76 69 6c 61 20 65 72 61 20 65 77 a0
  //   83 e4 83 e 57 0 a 6f 6f 66 4 a0 83 bf 20 eb 83 a8 53 0 a 72 61 62 a0 83 e4 83 e 5f 0 a 72 61 65 6c
  //   63 6 a0 83 bf 20 eb 83 e 47 c fc 8f 8b 83 e 3 9f 8b 7 9f b7 f0 a7 af a3 30 df 83 cf 83 d8 a3 c7 83
  //   de a7 f0 db 83 cf a3 c7 83 df 83 d8 7 84 3 9f 97 90 a3 84 20 43 fc 9f a3 d7 83 f1 9b 83 ea 48 90
  //    ← Keyboard
endmodule
